// Logisim project cpu.circ as structural Verilog: 9 circuits, main circuit main
module ULA (
  input  [7:0] A,
  input  [7:0] B,
  input  OP,
  output overflow__sem_sinal,
  output overflow__com_sinal,
  output O,
  output O_2,
  output O_3,
  output [7:0] R
);

  wire somador_1_c7, somador_1_c8;
  wire [7:0] xor_1_out;

  assign xor_1_out = {8{OP}} ^ B;  // XOR_Gate xor_1, 8 bits wide
  Somador somador_1 (.c0(OP), .A(A), .B(xor_1_out), .S(R), .c7(somador_1_c7), .c8(somador_1_c8));
  Comparador comparador_1 (.A(A), .B(B), .O(O), .O_2(O_2), .O_3(O_3));
  xor xor_2 (overflow__sem_sinal, OP, somador_1_c8);
  xor xor_3 (overflow__com_sinal, somador_1_c8, somador_1_c7);

  // Notes on the sheet:
  //   c0 = OP
  //   Circuito ULA: Recebe dois operandos de 8 bits (A e B), e um bit OP (0 para adição e 1 para subtração) e devolve R (o resultado
  //   da operação entre A e B), e outros 5 bits que indicam se houve overflow na interpretação sem sinal, se houve overflow na interpretação
  //   com sinal, se A = B, se A > B ou A < B
  //   inverte B se OP = 1
  //   somador
  //   Comparador
  //   c8 xor OP
  //   c8 xor c7
  //   indica se A = B
  //   indica se A > B
  //   indica se A < B
endmodule

module Somador (
  input  [7:0] A,
  input  [7:0] B,
  input  c0,
  output c7,
  output c8,
  output [7:0] S
);

  wire somabits_1_cout, somabits_2_cout, somabits_3_cout, somabits_4_cout, somabits_5_cout, somabits_6_cout;

  Somabits somabits_1 (.Cin(c0), .a(A[0]), .b(B[0]), .S(S[0]), .Cout(somabits_1_cout));
  Somabits somabits_2 (.Cin(somabits_1_cout), .a(A[1]), .b(B[1]), .S(S[1]), .Cout(somabits_2_cout));
  Somabits somabits_3 (.Cin(somabits_2_cout), .a(A[2]), .b(B[2]), .S(S[2]), .Cout(somabits_3_cout));
  Somabits somabits_4 (.Cin(somabits_5_cout), .a(A[4]), .b(B[4]), .S(S[4]), .Cout(somabits_4_cout));
  Somabits somabits_5 (.Cin(somabits_3_cout), .a(A[3]), .b(B[3]), .S(S[3]), .Cout(somabits_5_cout));
  Somabits somabits_6 (.Cin(somabits_4_cout), .a(A[5]), .b(B[5]), .S(S[5]), .Cout(somabits_6_cout));
  Somabits somabits_7 (.Cin(c7), .a(A[7]), .b(B[7]), .S(S[7]), .Cout(c8));
  Somabits somabits_8 (.Cin(somabits_6_cout), .a(A[6]), .b(B[6]), .S(S[6]), .Cout(c7));

  // Notes on the sheet:
  //   e devolve S = A + B se OP = 0
  //   ou devolve S = A - B se OP = 1
  //   também devolve os bits c7 e c8, que são os valores dos dois últimos carrys da operação
  //   Circuito Somador: recebe dois operandos de oito bits (A e B) e um bit OP
  //   <- somabits
endmodule

module Somabits (
  input  a,
  input  b,
  input  Cin,
  output Cout,
  output S
);

  wire and_1_out, and_2_out, xor_1_out;

  xor xor_1 (xor_1_out, a, b);
  xor xor_2 (S, Cin, xor_1_out);
  and and_1 (and_1_out, a, b);
  or or_1 (Cout, and_1_out, and_2_out);
  and and_2 (and_2_out, xor_1_out, Cin);

  // Notes on the sheet:
  //   Circuito somabits: Recebe três bits (a, b e Cin) e devolve
  //   S = (a xor b) xor Cin       e    Cout = [(a xor b)and Cin] or Cout
endmodule

module Comparador (
  input  [7:0] A,
  input  [7:0] B,
  output O,
  output O_2,
  output O_3
);

  wire compara4bits_1_o, compara4bits_1_o_2, compara4bits_1_o_3, compara4bits_2_o_2, compara4bits_2_o_3;

  Compara4bits compara4bits_1 (
    .i(1'b1), .A(A[7:4]), .B(B[7:4]), .O(compara4bits_1_o), .O_2(compara4bits_1_o_2), .O_3(compara4bits_1_o_3));
  Compara4bits compara4bits_2 (
    .i(compara4bits_1_o), .A(A[3:0]), .B(B[3:0]), .O(O), .O_2(compara4bits_2_o_2), .O_3(compara4bits_2_o_3));
  xor xor_1 (O_2, compara4bits_2_o_2, compara4bits_1_o_2);
  xor xor_2 (O_3, compara4bits_2_o_3, compara4bits_1_o_3);

  // Notes on the sheet:
  //   Compara4bits
  //   Compara4bits
  //   Comparador foi implementado com 2 Compara4bits. O primeiro compara A7A6A5A4 com B7B6B5B4, o segundo
  //   para O> se A > B ou 1 para O< se A < B ( apenas uma das três saídas recebe 1, as outras recebem 0).
  //   As comparações são referentes a interpretação sem sinal.
  //   compara A3A2A1A0 com B3B2B1B0
  //   Circuito Compara4bits: Recebe um bit i e 2 números de 4 bits ( A e B) e devolve outros 3 bits ( O=, O< e O>). Se i =1, devolve 1 para O= se A = B ou 1
endmodule

// AC
module main (
  input  [7:0] \Entrada_do_usuário ,
  input  [7:0] \Entrada_do_usuário_2 ,
  input  in_3
);

  wire _0, _1, _2, _3, _4, _5, _6, _7, _8, _9, _10, _11, _12, _13, _14, _15, and_1_out, and_2_out, and_3_out,
       clk, F_X, not_1_out, or_1_out, or_2_out, reset, ula_1_o, ula_1_o_2;
  wire [3:0] register_1_q, register_1_q_2;
  wire [7:0] AC_q, controlled_buffer_1_out, controlled_buffer_2_out, controlled_buffer_3_out,
       controlled_buffer_5_out, controlled_buffer_10_out, IR_q, IR_q_2, PC_q, ula_1_r;
  wire [15:0] controlled_buffer_6_out, controlled_buffer_7_out;
  wire [15:8] controlled_buffer_5_out_2;

  assign controlled_buffer_1_out = _9 ? controlled_buffer_5_out : 8'bz;  // Controlled_Buffer controlled_buffer_1
  assign controlled_buffer_2_out = or_1_out ? controlled_buffer_5_out_2 : 8'bz;  // Controlled_Buffer controlled_buffer_2
  or or_1 (or_1_out, _5, and_2_out, and_1_out);
  Hex_Digit_Display hex_digit_display_1 (.value(register_1_q_2));  // open: dp
  Button Reset_button (.out(reset));
  Register register_1 (.D(controlled_buffer_1_out), .Q({register_1_q_2, register_1_q}), .clk(clk));  // open: en, clr
  not not_1 (not_1_out, F_X);
  and and_1 (and_1_out, _6, ula_1_o_2);
  and and_2 (and_2_out, ula_1_o, _7);
  Hex_Digit_Display hex_digit_display_2 (.value(register_1_q));  // open: dp
  Counter PC (
    .load(or_1_out), .D(controlled_buffer_2_out), .count(not_1_out), .Q(PC_q), .clk(clk), .clr(or_2_out));  // open: carry
  or or_2 (or_2_out, _15, and_3_out);
  and and_3 (and_3_out, reset, F_X);
  assign controlled_buffer_3_out = _1 ? IR_q : 8'bz;  // Controlled_Buffer controlled_buffer_3
  assign controlled_buffer_3_out = _4 ? PC_q : 8'bz;  // Controlled_Buffer controlled_buffer_4
  Register #(.width(16)) IR (.D(controlled_buffer_6_out), .Q({IR_q_2, IR_q}), .clk(clk));  // open: en, clr
  assign {controlled_buffer_5_out_2, controlled_buffer_5_out} = _8 ? {{8{1'b0}}, \Entrada_do_usuário } : 16'bz;  // Controlled_Buffer controlled_buffer_5
  RAM #(.dataWidth(16)) ram_1 (
    .addr(controlled_buffer_3_out), .data({controlled_buffer_5_out_2, controlled_buffer_5_out}), .clk(clk),
    .ld(_10));  // open: sel, clr
  UC UC (
    .Fetch__execute(F_X), .\Código_de_instrução ({IR_q_2, IR_q}),
    .out_3({_15, _14, _13, _12, _11, _10, _9, _8, _7, _6, _5, _4, _3, _2, _1, _0}));
  assign controlled_buffer_6_out = _0 ? {controlled_buffer_5_out_2, controlled_buffer_5_out} : 16'bz;  // Controlled_Buffer controlled_buffer_6
  assign controlled_buffer_7_out = _2 ? {controlled_buffer_5_out_2, controlled_buffer_5_out} : 16'bz;  // Controlled_Buffer controlled_buffer_7
  assign controlled_buffer_7_out[7:0] = _13 ? ula_1_r : 8'bz;  // Controlled_Buffer controlled_buffer_8
  Register AC (.D(controlled_buffer_7_out[7:0]), .Q(AC_q), .clk(clk));  // open: en, clr
  assign {controlled_buffer_5_out_2, controlled_buffer_5_out} = _3 ? {{8{1'b0}}, AC_q} : 16'bz;  // Controlled_Buffer controlled_buffer_9
  Register register_2 (.D(\Entrada_do_usuário_2 ), .clk(in_3));  // open: en, Q, clr
  assign controlled_buffer_10_out = _12 ? {8{1'b0}} : 8'bz;  // Controlled_Buffer controlled_buffer_10
  assign controlled_buffer_10_out = _11 ? controlled_buffer_5_out : 8'bz;  // Controlled_Buffer controlled_buffer_11
  ULA ula_1 (
    .OP(_14), .A(AC_q), .B(controlled_buffer_10_out), .R(ula_1_r), .O(ula_1_o), .O_2(ula_1_o_2));  // open: overflow__sem_sinal, overflow__com_sinal, O_3
  Clock clock_1 (.out(clk));
  J_K_Flip_Flop j_k_ff_1 (.J(1'b1), .clk(clk), .K(1'b1), .Q(F_X));  // open: Qn, preset, en, reset
  // also tied to GND on the sheet: {controlled_buffer_7_out[8], controlled_buffer_7_out[9], controlled_buffer_7_out[10], controlled_buffer_7_out[11], controlled_buffer_7_out[12], controlled_buffer_7_out[13], controlled_buffer_7_out[14], controlled_buffer_7_out[15]}

  // Notes on the sheet:
  //   Saída
  //   Parte 4: cpu
  //   ----------------------------------------------
  //   [write/read]
  //   João Seckler, 4603521, joaoseckler@gmail.com
  //   Jose Eduardo R M Peres y Peres, 8945332, jose.peres@usp.br
  //   Gilvane da Silva Sousa, 10258726, gilvane.silva1@usp.br
  //   =
  //   >
  //   FLAGS
  //   0. RAM -> IR
  //   1. IR -> RAM
  //   2. RAM -> AC
  //   3. AC -> RAM
  //   4. PC -> RAM
  //   5. RAM -> PC (incond.)
  //   6. RAM -> PC if >
  //   7. RAM -> PC if =
  //   8. input -> RAM
  //   9. RAM -> output
  //   10. RAM [write/read]
  //   11. RAM -> ULA B
  //   12. 0x00 -> ULA B
  //   13. ULA R -> AC
  //   14. ULA OP [+/-]
  //   15. reset & stop PC
  //   F/X. 0= Fetch/ 1 = Execute
  //   Clock
  //   Esse FF controla se estamos
  //   em "fetch" ou "execute"
  //   A cada pulso, ele troca de 0 para 1
endmodule

module Comparabits (
  input  i,
  input  a,
  input  b,
  output O,
  output O_2,
  output O_3
);

  wire not_1_out, not_2_out, xnor_1_out;

  xnor xnor_1 (xnor_1_out, a, b);
  and and_1 (O_2, a, i, not_1_out);
  not not_1 (not_1_out, b);
  not not_2 (not_2_out, a);
  and and_2 (O_3, not_2_out, i, b);
  and and_3 (O, i, xnor_1_out);

  // Notes on the sheet:
  //   Circuito Comparabits: Recebe 3 bits ( a, b e i) e devolve outros 3 bits ( O=, O< e O>). Se i =1, devolve 1 para O= se a = b ou 1
  //   para O> se a > b ou 1 para O< se a < b ( apenas uma das três saídas recebe 1, as outras recebem 0).
  //   Também, se i=0, não compara os bits a e b, devolve 0 nas três saídas. As comparações são referentes a interpretação sem sinal.
  //   i AND ( a XNOR b)
  //   a AND ( NOT b)
  //   (NOT a) AND b
endmodule

module Compara2bits (
  input  [1:0] A,
  input  [1:0] B,
  input  i,
  output O,
  output O_2,
  output O_3
);

  wire comparabits_1_o, comparabits_1_o_2, comparabits_1_o_3, comparabits_2_o_2, comparabits_2_o_3;

  Comparabits comparabits_1 (
    .i(i), .a(A[1]), .b(B[1]), .O(comparabits_1_o), .O_2(comparabits_1_o_2), .O_3(comparabits_1_o_3));
  Comparabits comparabits_2 (
    .i(comparabits_1_o), .a(A[0]), .b(B[0]), .O(O), .O_2(comparabits_2_o_2), .O_3(comparabits_2_o_3));
  or or_1 (O_2, comparabits_2_o_2, comparabits_1_o_2);
  or or_2 (O_3, comparabits_2_o_3, comparabits_1_o_3);

  // Notes on the sheet:
  //   Comparabits
  //   Comparabits
  //   Compara2bits foi implementado com 2 Comparabits. O primeiro compara A1 e B1, o segundo compara A0 e B0.
  //   para O> se A > B ou 1 para O< se A < B ( apenas uma das três saídas recebe 1, as outras recebem 0).
  //   Também, se i=0, não compara A e B, devolve 0 nas três saídas. As comparações são referentes a interpretação sem sinal.
  //   Circuito Compara2bits: Recebe um bit i e 2 números de 2 bits ( A e B) e devolve outros 3 bits ( O=, O< e O>). Se i =1, devolve 1 para O= se A = B ou 1
  //   A = B
  //   A > B
  //   A < B
endmodule

module Compara4bits (
  input  [3:0] A,
  input  [3:0] B,
  input  i,
  output O,
  output O_2,
  output O_3
);

  wire compara2bits_1_o, compara2bits_1_o_2, compara2bits_1_o_3, compara2bits_2_o_2, compara2bits_2_o_3;

  Compara2bits compara2bits_1 (
    .i(i), .A(A[3:2]), .B(B[3:2]), .O(compara2bits_1_o), .O_2(compara2bits_1_o_2), .O_3(compara2bits_1_o_3));
  Compara2bits compara2bits_2 (
    .i(compara2bits_1_o), .A(A[1:0]), .B(B[1:0]), .O(O), .O_2(compara2bits_2_o_2), .O_3(compara2bits_2_o_3));
  or or_1 (O_2, compara2bits_2_o_2, compara2bits_1_o_2);
  or or_2 (O_3, compara2bits_2_o_3, compara2bits_1_o_3);

  // Notes on the sheet:
  //   Compara2bits
  //   Compara2bits
  //   para O> se A > B ou 1 para O< se A < B ( apenas uma das três saídas recebe 1, as outras recebem 0).
  //   Também, se i=0, não compara A e B, devolve 0 nas três saídas. As comparações são referentes a interpretação sem sinal.
  //   Compara4bits foi implementado com 2 Compara2bits. O primeiro compara A3A2 com B3B2, o segundo compara A1A0 com B1B0.
  //   Circuito Compara4bits: Recebe um bit i e 2 números de 4 bits ( A e B) e devolve outros 3 bits ( O=, O< e O>). Se i =1, devolve 1 para O= se A = B ou 1
  //   A = B
  //   A > B
  //   A < B
endmodule

module UC (
  input  Fetch__execute,
  input  [15:0] \Código_de_instrução ,
  output [15:0] out_3
);

  wire decoder_1_out1, decoder_1_out2, decoder_1_out3, decoder_1_out4, decoder_1_out7, decoder_1_out8,
       decoder_1_out9, decoder_1_out10, decoder_1_out11, decoder_1_out13, not_3_out, or_1_out, or_2_out,
       or_3_out, or_4_out, or_5_out;

  Decoder #(.select(4)) decoder_1 (
    .out1(decoder_1_out1), .out2(decoder_1_out2), .out3(decoder_1_out3), .out4(decoder_1_out4),
    .out7(decoder_1_out7), .out8(decoder_1_out8), .out9(decoder_1_out9), .out10(decoder_1_out10),
    .out11(decoder_1_out11), .out13(decoder_1_out13), .sel(\Código_de_instrução [11:8]));  // open: out0, out5, out6, out12, out14, out15, en
  or or_1 (or_1_out, decoder_1_out1, decoder_1_out2, decoder_1_out3, decoder_1_out4, decoder_1_out7, decoder_1_out8);
  or or_2 (or_2_out, decoder_1_out1, decoder_1_out3, decoder_1_out4, decoder_1_out8);
  or or_3 (or_3_out, decoder_1_out3, decoder_1_out4);
  or or_4 (or_4_out, decoder_1_out11, decoder_1_out13);
  or or_5 (or_5_out, decoder_1_out3, decoder_1_out4);
  not not_1 (out_3[0], Fetch__execute);
  and _1 (out_3[1], or_1_out, Fetch__execute);
  and _2 (out_3[2], decoder_1_out1, Fetch__execute);
  and _3 (out_3[3], decoder_1_out2, Fetch__execute);
  not not_2 (out_3[4], Fetch__execute);
  and _5 (out_3[5], decoder_1_out10, Fetch__execute);
  and _6 (out_3[6], decoder_1_out11, Fetch__execute);
  and _7 (out_3[7], decoder_1_out13, Fetch__execute);
  and _8 (out_3[8], decoder_1_out7, Fetch__execute);
  and _9 (out_3[9], decoder_1_out8, Fetch__execute);
  or _10 (out_3[10], or_2_out, not_3_out);
  not not_3 (not_3_out, Fetch__execute);
  and _11 (out_3[11], or_3_out, Fetch__execute);
  and _12 (out_3[12], or_4_out, Fetch__execute);
  and _13 (out_3[13], or_5_out, Fetch__execute);
  and _14 (out_3[14], decoder_1_out4, Fetch__execute);
  and _15 (out_3[15], decoder_1_out9, Fetch__execute);

  // Notes on the sheet:
  //   FLAGS
  //   0. RAM -> IR
  //   1. IR -> RAM
  //   2. RAM -> AC
  //   3. AC -> RAM
  //   4. PC -> RAM
  //   5. RAM -> PC (incond.)
  //   6. RAM -> PC if >
  //   7. RAM -> PC if =
  //   8. input -> RAM
  //   9. RAM -> output
  //   10. RAM [write/read]
  //   11. RAM -> ULA B
  //   12. 0x00 -> ULA B
  //   13. ULA R -> AC
  //   14. ULA OP [+/-]
  //   15. reset & stop PC
  //   F/X. 0= Fetch/ 1 = Execute
  //   1, 2, 3, 4
  //   7, 8, 9, 10, 11
  //   13
  //   0
  //   4
endmodule
