// Logisim project cpuV0.circ as structural Verilog: 8 circuits, main circuit main
module ULA (
  input  [7:0] A,
  input  [7:0] B,
  input  OP,
  output overflow__sem_sinal,
  output overflow__com_sinal,
  output O,
  output O_2,
  output O_3,
  output [7:0] R
);

  wire somador_1_c7, somador_1_c8;
  wire [7:0] xor_1_out;

  assign xor_1_out = {8{OP}} ^ B;  // XOR_Gate xor_1, 8 bits wide
  Somador somador_1 (.c0(OP), .A(A), .B(xor_1_out), .S(R), .c7(somador_1_c7), .c8(somador_1_c8));
  Comparador comparador_1 (.A(A), .B(B), .O(O), .O_2(O_2), .O_3(O_3));
  xor xor_2 (overflow__sem_sinal, OP, somador_1_c8);
  xor xor_3 (overflow__com_sinal, somador_1_c8, somador_1_c7);

  // Notes on the sheet:
  //   c0 = OP
  //   Circuito ULA: Recebe dois operandos de 8 bits (A e B), e um bit OP (0 para adição e 1 para subtração) e devolve R (o resultado
  //   da operação entre A e B), e outros 5 bits que indicam se houve overflow na interpretação sem sinal, se houve overflow na interpretação
  //   com sinal, se A = B, se A > B ou A < B
  //   inverte B se OP = 1
  //   somador
  //   Comparador
  //   c8 xor OP
  //   c8 xor c7
  //   indica se A = B
  //   indica se A > B
  //   indica se A < B
endmodule

module Somador (
  input  [7:0] A,
  input  [7:0] B,
  input  c0,
  output c7,
  output c8,
  output [7:0] S
);

  wire somabits_1_cout, somabits_2_cout, somabits_3_cout, somabits_4_cout, somabits_5_cout, somabits_6_cout;

  Somabits somabits_1 (.Cin(somabits_2_cout), .a(A[1]), .b(B[1]), .S(S[1]), .Cout(somabits_1_cout));
  Somabits somabits_2 (.Cin(c0), .a(A[0]), .b(B[0]), .S(S[0]), .Cout(somabits_2_cout));
  Somabits somabits_3 (.Cin(somabits_1_cout), .a(A[2]), .b(B[2]), .S(S[2]), .Cout(somabits_3_cout));
  Somabits somabits_4 (.Cin(somabits_3_cout), .a(A[3]), .b(B[3]), .S(S[3]), .Cout(somabits_4_cout));
  Somabits somabits_5 (.Cin(somabits_4_cout), .a(A[4]), .b(B[4]), .S(S[4]), .Cout(somabits_5_cout));
  Somabits somabits_6 (.Cin(somabits_5_cout), .a(A[5]), .b(B[5]), .S(S[5]), .Cout(somabits_6_cout));
  Somabits somabits_7 (.Cin(c7), .a(A[7]), .b(B[7]), .S(S[7]), .Cout(c8));
  Somabits somabits_8 (.Cin(somabits_6_cout), .a(A[6]), .b(B[6]), .S(S[6]), .Cout(c7));

  // Notes on the sheet:
  //   e devolve S = A + B se OP = 0
  //   ou devolve S = A - B se OP = 1
  //   também devolve os bits c7 e c8, que são os valores dos dois últimos carrys da operação
  //   Circuito Somador: recebe dois operandos de oito bits (A e B) e um bit OP
  //   <- somabits
endmodule

module Somabits (
  input  a,
  input  b,
  input  Cin,
  output Cout,
  output S
);

  wire and_1_out, and_2_out, xor_1_out;

  xor xor_1 (xor_1_out, a, b);
  xor xor_2 (S, Cin, xor_1_out);
  and and_1 (and_1_out, a, b);
  or or_1 (Cout, and_1_out, and_2_out);
  and and_2 (and_2_out, xor_1_out, Cin);

  // Notes on the sheet:
  //   Circuito somabits: Recebe três bits (a, b e Cin) e devolve
  //   S = (a xor b) xor Cin       e    Cout = [(a xor b)and Cin] or Cout
endmodule

module Comparador (
  input  [7:0] A,
  input  [7:0] B,
  output O,
  output O_2,
  output O_3
);

  wire compara4bits_1_o, compara4bits_1_o_2, compara4bits_1_o_3, compara4bits_2_o_2, compara4bits_2_o_3;

  Compara4bits compara4bits_1 (
    .i(1'b1), .A(A[7:4]), .B(B[7:4]), .O(compara4bits_1_o), .O_2(compara4bits_1_o_2), .O_3(compara4bits_1_o_3));
  Compara4bits compara4bits_2 (
    .i(compara4bits_1_o), .A(A[3:0]), .B(B[3:0]), .O(O), .O_2(compara4bits_2_o_2), .O_3(compara4bits_2_o_3));
  xor xor_1 (O_2, compara4bits_2_o_2, compara4bits_1_o_2);
  xor xor_2 (O_3, compara4bits_2_o_3, compara4bits_1_o_3);

  // Notes on the sheet:
  //   Compara4bits
  //   Compara4bits
  //   Comparador foi implementado com 2 Compara4bits. O primeiro compara A7A6A5A4 com B7B6B5B4, o segundo
  //   para O> se A > B ou 1 para O< se A < B ( apenas uma das três saídas recebe 1, as outras recebem 0).
  //   As comparações são referentes a interpretação sem sinal.
  //   compara A3A2A1A0 com B3B2B1B0
  //   Circuito Compara4bits: Recebe um bit i e 2 números de 4 bits ( A e B) e devolve outros 3 bits ( O=, O< e O>). Se i =1, devolve 1 para O= se A = B ou 1
endmodule

// AC
module main (
  input  reset_PC,
  input  Clear_RAM
);

  wire _0, _1, _2, _3, _4, _5, and_1_out, and_2_out, and_3_out, clk, decoder_1_out0, decoder_1_out1,
       decoder_1_out2, F_X, not_1_out, not_2_out, not_3_out, not_4_out, not_5_out, not_6_out, not_7_out,
       not_8_out, not_9_out, not_10_out, not_11_out, not_12_out, not_13_out, not_14_out, not_15_out,
       not_16_out, not_17_out, not_18_out;
  wire [7:0] AC_q, controlled_buffer_1_out, controlled_buffer_4_out, controlled_buffer_4_out_2, IR_q, IR_q_2,
       PC_q;
  wire [15:0] controlled_buffer_3_out, ram_1_data;

  Clock clock_1 (.out(clk));
  J_K_Flip_Flop j_k_ff_1 (.J(1'b1), .clk(clk), .K(1'b1), .Q(F_X));  // open: Qn, preset, en, reset
  Counter PC (.count(not_1_out), .Q(PC_q), .clk(clk), .clr(reset_PC));  // open: load, D, carry
  not not_1 (not_1_out, F_X);
  assign controlled_buffer_1_out = _4 ? PC_q : 8'bz;  // Controlled_Buffer controlled_buffer_1
  assign controlled_buffer_1_out = _1 ? IR_q : 8'bz;  // Controlled_Buffer controlled_buffer_2
  Register #(.width(16)) IR (.D(controlled_buffer_3_out), .Q({IR_q_2, IR_q}), .clk(clk));  // open: en, clr
  Decoder #(.select(2)) decoder_1 (
    .out0(decoder_1_out0), .out1(decoder_1_out1), .out2(decoder_1_out2), .sel(IR_q_2[1:0]));  // open: out3, en
  RAM #(.dataWidth(16)) ram_1 (
    .addr(controlled_buffer_1_out), .data(ram_1_data), .clk(clk), .ld(_5), .clr(Clear_RAM));  // open: sel
  assign controlled_buffer_3_out = _0 ? ram_1_data : 16'bz;  // Controlled_Buffer controlled_buffer_3
  Register AC (.D(controlled_buffer_4_out), .Q(AC_q), .clk(clk));  // open: en, clr
  assign {controlled_buffer_4_out_2, controlled_buffer_4_out} = _2 ? ram_1_data : 16'bz;  // Controlled_Buffer controlled_buffer_4
  assign ram_1_data = _3 ? {{8{1'b0}}, AC_q} : 16'bz;  // Controlled_Buffer controlled_buffer_5
  not not_2 (not_2_out, 1'b1);
  not not_3 (not_3_out, 1'b1);
  not not_4 (not_4_out, 1'b1);
  not not_5 (not_5_out, 1'b1);
  not not_6 (not_6_out, 1'b1);
  not not_7 (not_7_out, 1'b1);
  not not_8 (not_8_out, 1'b1);
  not not_9 (not_9_out, 1'b1);
  not not_10 (not_10_out, 1'b1);
  not not_11 (not_11_out, 1'b1);
  not not_12 (not_12_out, 1'b1);
  not not_13 (not_13_out, 1'b1);
  assign _5 = and_2_out ? 1'b1 : 1'bz;  // Controlled_Buffer controlled_buffer_6
  not not_14 (not_14_out, 1'b1);
  not not_15 (not_15_out, 1'b1);
  not not_16 (not_16_out, 1'b1);
  assign _5 = and_3_out ? not_17_out : 1'bz;  // Controlled_Buffer controlled_buffer_7
  not not_17 (not_17_out, 1'b1);
  assign _2 = not_18_out ? not_3_out : 1'bz;  // Controlled_Buffer controlled_buffer_8
  assign _3 = not_18_out ? not_4_out : 1'bz;  // Controlled_Buffer controlled_buffer_9
  assign _4 = not_18_out ? 1'b1 : 1'bz;  // Controlled_Buffer controlled_buffer_10
  assign _5 = not_18_out ? 1'b1 : 1'bz;  // Controlled_Buffer controlled_buffer_11
  assign _2 = and_1_out ? not_7_out : 1'bz;  // Controlled_Buffer controlled_buffer_12
  assign _3 = and_1_out ? not_8_out : 1'bz;  // Controlled_Buffer controlled_buffer_13
  assign _4 = and_1_out ? not_9_out : 1'bz;  // Controlled_Buffer controlled_buffer_14
  assign _5 = and_1_out ? not_10_out : 1'bz;  // Controlled_Buffer controlled_buffer_15
  assign _1 = and_2_out ? 1'b1 : 1'bz;  // Controlled_Buffer controlled_buffer_16
  assign _2 = and_2_out ? 1'b1 : 1'bz;  // Controlled_Buffer controlled_buffer_17
  assign _3 = and_2_out ? not_12_out : 1'bz;  // Controlled_Buffer controlled_buffer_18
  assign _4 = and_2_out ? not_13_out : 1'bz;  // Controlled_Buffer controlled_buffer_19
  assign _1 = and_3_out ? 1'b1 : 1'bz;  // Controlled_Buffer controlled_buffer_20
  assign _2 = and_3_out ? not_15_out : 1'bz;  // Controlled_Buffer controlled_buffer_21
  assign _3 = and_3_out ? 1'b1 : 1'bz;  // Controlled_Buffer controlled_buffer_22
  assign _4 = and_3_out ? not_16_out : 1'bz;  // Controlled_Buffer controlled_buffer_23
  assign _0 = not_18_out ? 1'b1 : 1'bz;  // Controlled_Buffer controlled_buffer_24
  assign _1 = not_18_out ? not_2_out : 1'bz;  // Controlled_Buffer controlled_buffer_25
  not not_18 (not_18_out, F_X);
  assign _0 = and_1_out ? not_5_out : 1'bz;  // Controlled_Buffer controlled_buffer_26
  assign _1 = and_1_out ? not_6_out : 1'bz;  // Controlled_Buffer controlled_buffer_27
  and and_1 (and_1_out, decoder_1_out0, F_X);
  assign _0 = and_2_out ? not_11_out : 1'bz;  // Controlled_Buffer controlled_buffer_28
  and and_2 (and_2_out, decoder_1_out1, F_X);
  assign _0 = and_3_out ? not_14_out : 1'bz;  // Controlled_Buffer controlled_buffer_29
  and and_3 (and_3_out, decoder_1_out2, F_X);
  // also tied to GND on the sheet: {controlled_buffer_4_out_2[0], controlled_buffer_4_out_2[1], controlled_buffer_4_out_2[2], controlled_buffer_4_out_2[3], controlled_buffer_4_out_2[4], controlled_buffer_4_out_2[5], controlled_buffer_4_out_2[6], controlled_buffer_4_out_2[7]}

  // Notes on the sheet:
  //   A cada pulso, ele troca de 0 para 1
  //   João Seckler, 4603521, joaoseckler@gmail.com
  //   Jose Eduardo R M Peres y Peres, 8945332, jose.peres@usp.br
  //   Gilvane da Silva Sousa, 10258726, gilvane.silva1@usp.br
  //   Esse FF controla se estamos em fetch ou execute
  //   Read/write
  //   Parte 3: cpu V zero
  //   0x00--
  //   0x01EE
  //   0x02EE
  //   Fetch
  //   copie [EE] para o AC
  //   NOP - No operation
  //   copie [AC] para a posição de enderço EE
  //   FLAGS
  //   5. RAM 0=write/1=read
  //   0. 0= RAM -/-> IR/ 1 = RAM -> IR
  //   1. 0=IR -/-> RAM addr/1= IR -> RAM addr
  //   2. 0=RAM -/-> AC/1 = RAM -> AC
  //   3. 0= AC -/-> RAM/ 1 = AC -> RAM
  //   4. 0= PC -/-> RAM/1= PC -> RAM
  //   F/X. 0= Fetch/ 1 = Execute
endmodule

module Comparabits (
  input  i,
  input  a,
  input  b,
  output O,
  output O_2,
  output O_3
);

  wire not_1_out, not_2_out, xnor_1_out;

  xnor xnor_1 (xnor_1_out, a, b);
  and and_1 (O_2, a, i, not_1_out);
  not not_1 (not_1_out, b);
  not not_2 (not_2_out, a);
  and and_2 (O_3, not_2_out, i, b);
  and and_3 (O, i, xnor_1_out);

  // Notes on the sheet:
  //   Circuito Comparabits: Recebe 3 bits ( a, b e i) e devolve outros 3 bits ( O=, O< e O>). Se i =1, devolve 1 para O= se a = b ou 1
  //   para O> se a > b ou 1 para O< se a < b ( apenas uma das três saídas recebe 1, as outras recebem 0).
  //   Também, se i=0, não compara os bits a e b, devolve 0 nas três saídas. As comparações são referentes a interpretação sem sinal.
  //   i AND ( a XNOR b)
  //   a AND ( NOT b)
  //   (NOT a) AND b
endmodule

module Compara2bits (
  input  [1:0] A,
  input  [1:0] B,
  input  i,
  output O,
  output O_2,
  output O_3
);

  wire comparabits_1_o, comparabits_1_o_2, comparabits_1_o_3, comparabits_2_o_2, comparabits_2_o_3;

  Comparabits comparabits_1 (
    .i(i), .a(A[1]), .b(B[1]), .O(comparabits_1_o), .O_2(comparabits_1_o_2), .O_3(comparabits_1_o_3));
  Comparabits comparabits_2 (
    .i(comparabits_1_o), .a(A[0]), .b(B[0]), .O(O), .O_2(comparabits_2_o_2), .O_3(comparabits_2_o_3));
  or or_1 (O_2, comparabits_2_o_2, comparabits_1_o_2);
  or or_2 (O_3, comparabits_2_o_3, comparabits_1_o_3);

  // Notes on the sheet:
  //   Comparabits
  //   Comparabits
  //   Compara2bits foi implementado com 2 Comparabits. O primeiro compara A1 e B1, o segundo compara A0 e B0.
  //   para O> se A > B ou 1 para O< se A < B ( apenas uma das três saídas recebe 1, as outras recebem 0).
  //   Também, se i=0, não compara A e B, devolve 0 nas três saídas. As comparações são referentes a interpretação sem sinal.
  //   Circuito Compara2bits: Recebe um bit i e 2 números de 2 bits ( A e B) e devolve outros 3 bits ( O=, O< e O>). Se i =1, devolve 1 para O= se A = B ou 1
  //   A = B
  //   A > B
  //   A < B
endmodule

module Compara4bits (
  input  [3:0] A,
  input  [3:0] B,
  input  i,
  output O,
  output O_2,
  output O_3
);

  wire compara2bits_1_o, compara2bits_1_o_2, compara2bits_1_o_3, compara2bits_2_o_2, compara2bits_2_o_3;

  Compara2bits compara2bits_1 (
    .i(i), .A(A[3:2]), .B(B[3:2]), .O(compara2bits_1_o), .O_2(compara2bits_1_o_2), .O_3(compara2bits_1_o_3));
  Compara2bits compara2bits_2 (
    .i(compara2bits_1_o), .A(A[1:0]), .B(B[1:0]), .O(O), .O_2(compara2bits_2_o_2), .O_3(compara2bits_2_o_3));
  or or_1 (O_2, compara2bits_2_o_2, compara2bits_1_o_2);
  or or_2 (O_3, compara2bits_2_o_3, compara2bits_1_o_3);

  // Notes on the sheet:
  //   Compara2bits
  //   Compara2bits
  //   para O> se A > B ou 1 para O< se A < B ( apenas uma das três saídas recebe 1, as outras recebem 0).
  //   Também, se i=0, não compara A e B, devolve 0 nas três saídas. As comparações são referentes a interpretação sem sinal.
  //   Compara4bits foi implementado com 2 Compara2bits. O primeiro compara A3A2 com B3B2, o segundo compara A1A0 com B1B0.
  //   Circuito Compara4bits: Recebe um bit i e 2 números de 4 bits ( A e B) e devolve outros 3 bits ( O=, O< e O>). Se i =1, devolve 1 para O= se A = B ou 1
  //   A = B
  //   A > B
  //   A < B
endmodule
