// Logisim project somador.circ as structural Verilog: 5 circuits, main circuit main
module main (
  input  [7:0] A,
  input  [7:0] B,
  input  OP,
  output overflow__sem_sinal,
  output overflow__com_sinal,
  output [7:0] R
);

  wire somador_c7;
  wire [7:0] soma_subtr_1_out_3;

  somador somador (.c0(1'b0), .A(A), .B(soma_subtr_1_out_3), .S(R), .c7(somador_c7), .c8(overflow__sem_sinal));
  soma_subtr soma_subtr_1 (.Soa_ou_subtr(OP), .in_1(B), .out_3(soma_subtr_1_out_3));
  xor xor_1 (overflow__com_sinal, somador_c7, overflow__sem_sinal);

  // Notes on the sheet:
  //   João Seckler, 4603521, joaoseckler@gmail.com
  //   Gilvane da Silva Sousa, 10258726, gilvane.silva1@usp.br
  //   Jose Eduardo R M Peres y Peres, 8945332, jose.peres@usp.br
  //   Parte 1: Circuito Somador
  //   Circuito para adição e subtração de números de 8 bits
endmodule

module somador (
  input  [7:0] A,
  input  [7:0] B,
  input  c0,
  output c7,
  output c8,
  output [7:0] S
);

  wire somabits_1_cout, somabits_2_cout, somabits_3_cout, somabits_4_cout, somabits_5_cout, somabits_6_cout;

  somabits somabits_1 (.Cin(c0), .x(A[0]), .y(B[0]), .S(S[0]), .Cout(somabits_1_cout));
  somabits somabits_2 (.Cin(somabits_1_cout), .x(A[1]), .y(B[1]), .S(S[1]), .Cout(somabits_2_cout));
  somabits somabits_3 (.Cin(somabits_2_cout), .x(A[2]), .y(B[2]), .S(S[2]), .Cout(somabits_3_cout));
  somabits somabits_4 (.Cin(somabits_3_cout), .x(A[3]), .y(B[3]), .S(S[3]), .Cout(somabits_4_cout));
  somabits somabits_5 (.Cin(somabits_4_cout), .x(A[4]), .y(B[4]), .S(S[4]), .Cout(somabits_5_cout));
  somabits somabits_6 (.Cin(somabits_5_cout), .x(A[5]), .y(B[5]), .S(S[5]), .Cout(somabits_6_cout));
  somabits somabits_7 (.Cin(c7), .x(A[7]), .y(B[7]), .S(S[7]), .Cout(c8));
  somabits somabits_8 (.Cin(somabits_6_cout), .x(A[6]), .y(B[6]), .S(S[6]), .Cout(c7));
endmodule

module somabits (
  input  x,
  input  y,
  input  Cin,
  output Cout,
  output S
);

  wire and_1_out, and_2_out, xor_1_out;

  xor xor_1 (xor_1_out, x, y);
  xor xor_2 (S, Cin, xor_1_out);
  and and_1 (and_1_out, y, x);
  or or_1 (Cout, and_1_out, and_2_out);
  and and_2 (and_2_out, xor_1_out, Cin);
endmodule

module complemento (
  input  [7:0] in_1,
  output [7:0] out_2
);

  wire [7:0] not_1_out;

  assign not_1_out = ~in_1;  // NOT_Gate not_1, 8 bits wide
  somador somador_1 (.c0(1'b0), .A(not_1_out), .B(8'h1), .S(out_2));  // open: c7, c8

  // Notes on the sheet:
  //   complemento de 1
  //   + 1 (somador)
  //   1
  //   complemento de 2
endmodule

module soma_subtr (
  input  [7:0] in_1,
  input  Soa_ou_subtr,
  output [7:0] out_3
);

  wire [7:0] and_1_out, and_2_out, complemento_1_out_2, not_1_out;

  assign not_1_out = ~{8{Soa_ou_subtr}};  // NOT_Gate not_1, 8 bits wide
  assign and_1_out = not_1_out & in_1;  // AND_Gate and_1, 8 bits wide
  assign and_2_out = in_1 & {8{Soa_ou_subtr}};  // AND_Gate and_2, 8 bits wide
  complemento complemento_1 (.in_1(and_2_out), .out_2(complemento_1_out_2));
  assign out_3 = and_1_out | complemento_1_out_2;  // OR_Gate or_1, 8 bits wide

  // Notes on the sheet:
  //   complemento de 2
endmodule
